# Fritzing sketch Main Circuit (saved by Fritzing 0.9.2b)
circuit board: 8.46667cm x 5.64444cm
breadboards: 1

parts:
  Nano = Arduino Nano (Rev3.0)
  D1 = Rectifier Diode [part_number=1N4001 package="300 mil [THT]"]
  DHT1 = DHT11 Humitidy and Temperature Sensor
  LED1 = LED - 5mm [color="Red (633nm)" package="5 mm [THT]"]
  R3 = Resistor [tolerance=±5% resistance=220 package=THT]
  JACK1 = 2.1mm DC Barrel Jack
  U2 = RELAY [package=relay-t9a]
  JP1 = Header 2 [package=screwterminal-3.5mm-2_lock]
  R1 = Resistor [tolerance=±5% resistance=220 package=THT]
  R5 = Resistor [tolerance=±5% resistance=220 package=THT]
  Q1 = NPN-Transistor [package="TO92 [THT]"]
  JP2 = Header 1 [package=snap-female]
  JP3 = Header 1 [package=snap-female]
  JP4 = Header 1 [package=snap-female]
  JP5 = Header 1 [package=snap-female]
  JP6 = Header 1 [package=snap-female]
  R4 = Resistor [tolerance=±5% resistance=1k package=THT]
  JP7 = Header 1 [package=snap-female]

nets:
  GND: Nano.GND, DHT1.GND, LED1.cathode, JACK1.switch, JACK1.sleeve, JP1.1, Q1.E, JP3.1
  N1: Nano.D2, DHT1.DATA, R1.Pin_0
  N2: Nano.D8, JP5.1
  N3: Nano.D9, JP7.1
  N4: Nano.D10, R4.Pin_1
  N5: Nano.VIN, JACK1.center, U2.MAIN
  5V: Nano.5V, D1.cathode, DHT1.VDD, U2.COIL1, R1.Pin_1, JP2.1
  N6: Nano.A5, JP4.1
  N7: Nano.A4, JP6.1
  N8: D1.anode, U2.COIL2, Q1.C
  N9: LED1.anode, R3.Pin_1
  N10: R3.Pin_0, R5.Pin_1
  N11: U2.NC, JP1.2, R5.Pin_0
  N12: Q1.B, R4.Pin_0

custom parts:
  DHT11 Humitidy and Temperature Sensor: DHT11 Humidity and Temperature Sensor
  2.1mm DC Barrel Jack: 2.1mm DC Barrel Jack with Thru-Hole Connectors (breadboardable)
