# Fritzing sketch Screen Circuit (saved by Fritzing 0.9.2b)
circuit board: 8.46667cm x 5.64444cm
breadboards: 1

parts:
  S1 = Pushbutton [package="[THT]"]
  S2 = Pushbutton [package="[THT]"]
  Squix1 = OLED 0.96" 128x64 I2C SSD1306
  JP2 = Header 1 [package=snap-female]
  JP3 = Header 1 [package=snap-female]
  JP4 = Header 1 [package=snap-female]
  JP5 = Header 1 [package=snap-female]
  JP6 = Header 1 [package=snap-female]
  JP7 = Header 1 [package=snap-female]
  R6 = Resistor [tolerance=±5% resistance=10k package=THT]
  R7 = Resistor [tolerance=±5% resistance=10k package=THT]

nets:
  N1: S1.Pin_1, S1.Pin_2, S2.Pin_1, S2.Pin_2, Squix1.VCC, JP2.1
  N2: S1.Pin_3, S1.Pin_4, JP3.1, R6.Pin_1
  N3: S2.Pin_3, S2.Pin_4, JP7.1, R7.Pin_1
  N4: Squix1.GND, JP5.1, R6.Pin_0, R7.Pin_0
  N5: Squix1.SCL, JP4.1
  N6: Squix1.SCA, JP6.1
